// Logisim project gov.circ as structural Verilog: 1 circuit, main circuit main
module main (
  input  drop,
  input  run,
  input  mst_vld,
  input  slv_rdy,
  input  drop_log,
  input  log_rdy,
  input  inj_vld,
  output slv_vld,
  output mst_rdy,
  output log_vld,
  output inj_rdy
);

  wire and_2_out, and_4_out, and_5_out, and_6_out, and_7_out, or_1_out, or_2_out;

  and and_1 (mst_rdy, or_2_out, or_1_out);
  and and_2 (and_2_out, mst_vld, or_1_out);
  or or_1 (or_1_out, drop_log, log_rdy);
  and and_3 (log_vld, mst_vld, mst_rdy, ~drop_log);  // AND_Gate
  or or_2 (or_2_out, drop, and_4_out);
  and and_4 (and_4_out, run, and_6_out);
  and and_5 (and_5_out, run, and_2_out);
  and and_6 (and_6_out, slv_rdy, ~inj_vld);  // AND_Gate
  and and_7 (and_7_out, and_5_out, ~drop);  // AND_Gate
  or or_3 (slv_vld, and_7_out, inj_vld);

  assign inj_rdy = slv_rdy;
endmodule
