// Logisim project gov4.circ as structural Verilog: 1 circuit, main circuit main
module main (
  input  pause,
  input  drop,
  input  mst_vld,
  input  slv_rdy,
  input  drop_log,
  input  log_rdy,
  input  inj_vld,
  output slv_vld,
  output mst_rdy,
  output log_vld,
  output inj_rdy
);

  wire and_2_out, and_3_out, and_4_out, and_6_out, and_7_out, and_8_out, or_1_out, or_2_out;

  and and_1 (mst_rdy, ~pause, and_4_out);  // AND_Gate
  LED A (.in(and_2_out));
  and and_2 (and_2_out, ~pause, mst_vld);  // AND_Gate
  LED B (.in(and_4_out));
  and and_3 (and_3_out, and_2_out, or_2_out);
  and and_4 (and_4_out, or_2_out, or_1_out);
  LED C (.in(and_3_out));
  and and_5 (log_vld, and_3_out, ~drop_log);  // AND_Gate
  and and_6 (and_6_out, and_2_out, or_1_out);
  LED D (.in(or_1_out));
  or or_1 (or_1_out, drop_log, log_rdy);
  LED E (.in(and_6_out));
  LED F (.in(or_2_out));
  or or_2 (or_2_out, drop, and_8_out);
  and and_7 (and_7_out, ~drop, and_6_out);  // AND_Gate
  and and_8 (and_8_out, slv_rdy, ~inj_vld);  // AND_Gate
  or or_3 (slv_vld, and_7_out, inj_vld);

  assign inj_rdy = slv_rdy;
endmodule
